# Fritzing sketch circuit diagram (saved by Fritzing 0.9.3b)

parts:
  M1 = 1 chan 5v relay module
  M2 = DOIT Esp32 DevKit v1 (30 pins long, 11 pins width) [part_number=ESP32S-PIN30]
  Keypad4x2 = Keypad Membran 4x4
  JACK1 = 2.1mm Barrel Jack with Terminal Block
  JACK2 = 2.1mm Barrel Jack with Terminal Block
  L1 = Solenoid

nets:
  N1: M1.pin_1, JACK1.POS
  N2: M1.pin_2, M2.GND, JACK1.NEG
  N3: M1.pin_3, M2.D2
  N4: M1.pin_4, L1.pin2
  N5: M1.pin_5, JACK2.POS
  N6: M2.D4, Keypad4x2.Pin5
  N7: M2.D5, Keypad4x2.Pin6
  N8: M2.D18, Keypad4x2.Pin7
  N9: M2.D19, Keypad4x2.Pin8
  N10: M2.D27, Keypad4x2.Pin4
  N11: M2.D14, Keypad4x2.Pin3
  N12: M2.D12, Keypad4x2.Pin2
  N13: M2.D13, Keypad4x2.Pin1
  N14: JACK2.NEG, L1.pin1

custom parts:
  1 chan 5v relay module: 1 Channel 5V Relay Module Board Shield with Optocoupler Support High and Low Level Trigger for Arduino.
  DOIT Esp32 DevKit v1 (30 pins long, 11 pins width): The DOIT Esp32 DevKit v1 is one of the development board created by DOIT to evaluate the ESP-WROOM-32 module. It is based on the ESP32 microcontroller that boasts Wifi, Bluetooth, Ethernet and Low Power support all in a single chip. (vanepp) made breadboard work, adjusted pin numbering and labels and reduced size of schematic and cleaned up pcb. This chip is 30pins long (2 x15) and 11 pins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
  Keypad Membran 4x4: Membrane Keypad 4x4 Matrix
